// Logisim project traffic light.circ as structural Verilog: 12 circuits, main circuit newState
module _32delay (
  input  in_1,
  output out_2,
  output out_3,
  output out_4,
  output out_5,
  output out_6
);

  wire clock_1_out;

  Clock clock_1 (.out(clock_1_out));
  J_K_Flip_Flop #(.trigger("falling")) j_k_ff_1 (
    .J(in_1), .clk(clock_1_out), .K(in_1), .Q(out_6));  // open: Qn, preset, en, reset
  J_K_Flip_Flop #(.trigger("falling")) j_k_ff_2 (
    .J(in_1), .clk(out_6), .K(in_1), .Q(out_5));  // open: Qn, preset, en, reset
  J_K_Flip_Flop #(.trigger("falling")) j_k_ff_3 (
    .J(in_1), .clk(out_5), .K(in_1), .Q(out_4));  // open: Qn, preset, en, reset
  J_K_Flip_Flop #(.trigger("falling")) j_k_ff_4 (
    .J(in_1), .clk(out_4), .K(in_1), .Q(out_3));  // open: Qn, preset, en, reset
  J_K_Flip_Flop #(.trigger("falling")) j_k_ff_5 (
    .J(in_1), .clk(out_3), .K(in_1), .Q(out_2));  // open: Qn, preset, en, reset
endmodule

module circuit (
  input  a,
  input  b,
  input  c,
  input  d,
  input  e,
  output y
);

  wire and_1_out, and_2_out, not_1_out;

  not not_1 (not_1_out, c);
  and and_1 (and_1_out, b, c, d, e);
  and and_2 (and_2_out, a, not_1_out, d, e);
  or or_1 (y, and_1_out, and_2_out);
endmodule

module newState (
  input  in_1,
  output y
);

  wire and_1_out, and_2_out, and_3_out, and_4_out, and_5_out, and_6_out, and_7_out, and_8_out, and_9_out,
       and_10_out, and_11_out, clock_1_out, d_ff_1_q, d_ff_2_q, displaytimer2_1_a, displaytimer2_1_b,
       displaytimer2_1_c, displaytimer2_1_d, displaytimer2_1_e, displaytimer2_1_f, displaytimer2_1_g,
       displaytimer_1_a, displaytimer_1_b, displaytimer_1_c, displaytimer_1_d, displaytimer_1_e,
       displaytimer_1_f, displaytimer_1_g, n2bitcounter_1_out_2, n2bitcounter_1_out_3, n2bitcounter_2_out_2,
       n2bitcounter_2_out_3, n2bitcounter_3_out_2, n2bitcounter_3_out_3, n3bitcounter_1_out_2,
       n3bitcounter_1_out_3, n3bitcounter_1_out_4, n4bitdisplay1_1_a, n4bitdisplay1_1_b, n4bitdisplay1_1_c,
       n4bitdisplay1_1_d, n4bitdisplay1_1_e, n4bitdisplay1_1_f, n4bitdisplay1_1_g, n4bitdisplay_1_a,
       n4bitdisplay_1_b, n4bitdisplay_1_c, n4bitdisplay_1_d, n4bitdisplay_1_e, n4bitdisplay_1_f,
       n4bitdisplay_1_g, n4seconds_1_a, n4seconds_1_b, n4seconds_1_c, n4seconds_1_d, n4seconds_1_e,
       n4seconds_1_f, n4seconds_1_g, n4seconds_2_a, n4seconds_2_b, n4seconds_2_c, n4seconds_2_d,
       n4seconds_2_e, n4seconds_2_f, n4seconds_2_g, n4seconds_3_a, n4seconds_3_b, n4seconds_3_c,
       n4seconds_3_d, n4seconds_3_e, n4seconds_3_f, n4seconds_3_g, n8seconds_1_a, n8seconds_1_b,
       n8seconds_1_c, n8seconds_1_d, n8seconds_1_e, n8seconds_1_f, n8seconds_1_g, n16_second_display_1_out_2,
       n16_second_display_1_out_3, n16_second_display_1_out_4, n16_second_display_1_out_5, n32delay_1_out_2,
       n32delay_1_out_3, n32delay_1_out_4, n32delay_1_out_5, n32delay_1_out_6, not_1_out, not_2_out,
       not_3_out, not_4_out, not_5_out, not_6_out, not_7_out, not_8_out, not_9_out, not_10_out, not_11_out,
       or_1_out, or_2_out;

  _32delay u_32delay_1 (
    .in_1(in_1), .out_2(n32delay_1_out_2), .out_3(n32delay_1_out_3), .out_4(n32delay_1_out_4),
    .out_5(n32delay_1_out_5), .out_6(n32delay_1_out_6));
  not not_1 (not_1_out, n32delay_1_out_4);
  not not_2 (not_2_out, d_ff_1_q);
  not not_3 (not_3_out, d_ff_2_q);
  not not_4 (not_4_out, y);
  not not_5 (not_5_out, d_ff_2_q);
  not not_6 (not_6_out, y);
  and and_1 (and_1_out, n32delay_1_out_3, n32delay_1_out_4, n32delay_1_out_5, n32delay_1_out_6);
  and and_2 (and_2_out, n32delay_1_out_2, not_1_out, n32delay_1_out_5, n32delay_1_out_6);
  displaytimer2 displaytimer2_1 (
    .r(n32delay_1_out_2), .w(n32delay_1_out_3), .x(n32delay_1_out_4), .y(n32delay_1_out_5),
    .z(n32delay_1_out_6), .a(displaytimer2_1_a), .b(displaytimer2_1_b), .c(displaytimer2_1_c),
    .d(displaytimer2_1_d), .e(displaytimer2_1_e), .f(displaytimer2_1_f), .g(displaytimer2_1_g));
  displaytimer displaytimer_1 (
    .r(n32delay_1_out_2), .w(n32delay_1_out_3), .x(n32delay_1_out_4), .y(n32delay_1_out_5),
    .z(n32delay_1_out_6), .a(displaytimer_1_a), .b(displaytimer_1_b), .c(displaytimer_1_c),
    .d(displaytimer_1_d), .e(displaytimer_1_e), .f(displaytimer_1_f), .g(displaytimer_1_g));
  and and_3 (and_3_out, not_2_out, d_ff_2_q, y);
  or or_1 (or_1_out, and_3_out, and_4_out, and_5_out);
  and and_4 (and_4_out, d_ff_1_q, not_3_out);
  and and_5 (and_5_out, d_ff_1_q, not_4_out);
  and and_6 (and_6_out, not_5_out, y);
  or or_2 (or_2_out, and_6_out, and_7_out);
  and and_7 (and_7_out, d_ff_2_q, not_6_out);
  Clock clock_1 (.out(clock_1_out));
  or or_3 (y, and_1_out, and_2_out);
  _7_Segment_Display u_7_segment_display_1 (
    .g(displaytimer2_1_g), .f(displaytimer2_1_f), .a(displaytimer2_1_a), .b(displaytimer2_1_b),
    .e(displaytimer2_1_e), .d(displaytimer2_1_d), .c(displaytimer2_1_c));  // open: dp
  _7_Segment_Display u_7_segment_display_2 (
    .g(displaytimer_1_g), .f(displaytimer_1_f), .a(displaytimer_1_a), .b(displaytimer_1_b),
    .e(displaytimer_1_e), .d(displaytimer_1_d), .c(displaytimer_1_c));  // open: dp
  D_Flip_Flop d_ff_1 (.clk(clock_1_out), .D(or_1_out), .Q(d_ff_1_q));  // open: Qn, preset, en, reset
  D_Flip_Flop d_ff_2 (.clk(clock_1_out), .D(or_2_out), .Q(d_ff_2_q));  // open: Qn, preset, en, reset
  not not_7 (not_7_out, d_ff_1_q);
  _16_second_display u_16_second_display_1 (
    .in_1(in_1), .out_2(n16_second_display_1_out_2), .out_3(n16_second_display_1_out_3),
    .out_4(n16_second_display_1_out_4), .out_5(n16_second_display_1_out_5));
  and and_8 (and_8_out, ~d_ff_1_q, d_ff_2_q);  // AND_Gate
  and and_9 (and_9_out, ~d_ff_1_q, ~d_ff_2_q);  // AND_Gate
  and and_10 (and_10_out, d_ff_1_q, d_ff_2_q);
  and and_11 (and_11_out, d_ff_1_q, ~d_ff_2_q);  // AND_Gate
  not not_8 (not_8_out, n16_second_display_1_out_2);
  not not_9 (not_9_out, n16_second_display_1_out_3);
  not not_10 (not_10_out, n16_second_display_1_out_4);
  not not_11 (not_11_out, n16_second_display_1_out_5);
  _4bitdisplay1 u_4bitdisplay1_1 (
    .w(not_8_out), .x(not_9_out), .y(not_10_out), .z(not_11_out), .a(n4bitdisplay1_1_a),
    .b(n4bitdisplay1_1_b), .c(n4bitdisplay1_1_c), .d(n4bitdisplay1_1_d), .e(n4bitdisplay1_1_e),
    .f(n4bitdisplay1_1_f), .g(n4bitdisplay1_1_g));
  _7_Segment_Display u_7_segment_display_3 (
    .g(n4bitdisplay1_1_g), .f(n4bitdisplay1_1_f), .a(n4bitdisplay1_1_a), .b(n4bitdisplay1_1_b),
    .e(n4bitdisplay1_1_e), .d(n4bitdisplay1_1_d), .c(n4bitdisplay1_1_c));  // open: dp
  _2bitcounter u_2bitcounter_1 (.in_1(and_8_out), .out_2(n2bitcounter_1_out_2), .out_3(n2bitcounter_1_out_3));
  _4bitdisplay u_4bitdisplay_1 (
    .w(not_8_out), .x(not_9_out), .y(not_10_out), .z(not_11_out), .a(n4bitdisplay_1_a), .b(n4bitdisplay_1_b),
    .c(n4bitdisplay_1_c), .d(n4bitdisplay_1_d), .e(n4bitdisplay_1_e), .f(n4bitdisplay_1_f),
    .g(n4bitdisplay_1_g));
  _4seconds u_4seconds_1 (
    .w(n2bitcounter_1_out_2), .x(n2bitcounter_1_out_3), .a(n4seconds_1_a), .b(n4seconds_1_b),
    .c(n4seconds_1_c), .d(n4seconds_1_d), .e(n4seconds_1_e), .f(n4seconds_1_f), .g(n4seconds_1_g));
  _7_Segment_Display u_7_segment_display_4 (
    .g(n4bitdisplay_1_g), .f(n4bitdisplay_1_f), .a(n4bitdisplay_1_a), .b(n4bitdisplay_1_b),
    .e(n4bitdisplay_1_e), .d(n4bitdisplay_1_d), .c(n4bitdisplay_1_c));  // open: dp
  _7_Segment_Display u_7_segment_display_5 (
    .g(n4seconds_1_g), .f(n4seconds_1_f), .a(n4seconds_1_a), .b(n4seconds_1_b), .e(n4seconds_1_e),
    .d(n4seconds_1_d), .c(n4seconds_1_c));  // open: dp
  LED led_1 (.in(not_7_out));
  LED led_2 (.in(and_10_out));
  LED led_3 (.in(and_11_out));
  LED led_4 (.in(d_ff_1_q));
  LED led_5 (.in(and_8_out));
  LED led_6 (.in(and_9_out));
  LED led_7 (.in(d_ff_1_q));
  LED led_8 (.in(and_8_out));
  LED led_9 (.in(and_9_out));
  _3bitcounter u_3bitcounter_1 (
    .in_1(and_11_out), .out_2(n3bitcounter_1_out_2), .out_3(n3bitcounter_1_out_3),
    .out_4(n3bitcounter_1_out_4));
  _2bitcounter u_2bitcounter_2 (.in_1(and_8_out), .out_2(n2bitcounter_2_out_2), .out_3(n2bitcounter_2_out_3));
  _8seconds u_8seconds_1 (
    .w(n3bitcounter_1_out_2), .x(n3bitcounter_1_out_3), .y(n3bitcounter_1_out_4), .a(n8seconds_1_a),
    .b(n8seconds_1_b), .c(n8seconds_1_c), .d(n8seconds_1_d), .e(n8seconds_1_e), .f(n8seconds_1_f),
    .g(n8seconds_1_g));
  _4seconds u_4seconds_2 (
    .w(n2bitcounter_2_out_2), .x(n2bitcounter_2_out_3), .a(n4seconds_2_a), .b(n4seconds_2_b),
    .c(n4seconds_2_c), .d(n4seconds_2_d), .e(n4seconds_2_e), .f(n4seconds_2_f), .g(n4seconds_2_g));
  _7_Segment_Display u_7_segment_display_6 (
    .g(n8seconds_1_g), .f(n8seconds_1_f), .a(n8seconds_1_a), .b(n8seconds_1_b), .e(n8seconds_1_e),
    .d(n8seconds_1_d), .c(n8seconds_1_c));  // open: dp
  _7_Segment_Display u_7_segment_display_7 (
    .g(n4seconds_2_g), .f(n4seconds_2_f), .a(n4seconds_2_a), .b(n4seconds_2_b), .e(n4seconds_2_e),
    .d(n4seconds_2_d), .c(n4seconds_2_c));  // open: dp
  LED led_10 (.in(not_7_out));
  LED led_11 (.in(and_10_out));
  LED led_12 (.in(and_11_out));
  _2bitcounter u_2bitcounter_3 (.in_1(and_10_out), .out_2(n2bitcounter_3_out_2), .out_3(n2bitcounter_3_out_3));
  _4seconds u_4seconds_3 (
    .w(n2bitcounter_3_out_2), .x(n2bitcounter_3_out_3), .a(n4seconds_3_a), .b(n4seconds_3_b),
    .c(n4seconds_3_c), .d(n4seconds_3_d), .e(n4seconds_3_e), .f(n4seconds_3_f), .g(n4seconds_3_g));
  _7_Segment_Display u_7_segment_display_8 (
    .g(n4seconds_3_g), .f(n4seconds_3_f), .a(n4seconds_3_a), .b(n4seconds_3_b), .e(n4seconds_3_e),
    .d(n4seconds_3_d), .c(n4seconds_3_c));  // open: dp

  // Notes on the sheet:
  //   32 bit counter
  //   Timer T =1 for 16,16(+4),16(+8),16(+4)
  //   Timer Display 
  //   Changing states
  //   Logic for lights
  //   yellow timer
  //   East-West road
  //   North-South Road
  //   Indication of time to wait until green
endmodule

module displaytimer (
  input  r,
  input  w,
  input  x,
  input  y,
  input  z,
  output a,
  output b,
  output c,
  output d,
  output e,
  output f,
  output g
);

  wire and_1_out, and_2_out, and_3_out, and_4_out, and_5_out, and_6_out, and_7_out, and_8_out, and_9_out,
       and_10_out, and_11_out, and_12_out, and_13_out, and_14_out, and_15_out, and_16_out, and_17_out,
       and_18_out, and_19_out, and_20_out, and_21_out, and_22_out, and_23_out, and_24_out, and_25_out,
       and_26_out, and_27_out, and_28_out, and_29_out, and_30_out, and_31_out, and_32_out, and_33_out,
       and_34_out, and_35_out, and_36_out, and_37_out, and_38_out, and_39_out, and_40_out, and_41_out,
       and_42_out, and_43_out, and_44_out, and_45_out, and_46_out, and_47_out, and_48_out, and_49_out,
       and_50_out, and_51_out, and_52_out, and_53_out, and_54_out, and_55_out, and_56_out, not_1_out,
       not_2_out, not_3_out, not_4_out, not_5_out, not_6_out, not_7_out, not_8_out, not_9_out, not_10_out,
       not_11_out, not_12_out, not_13_out, not_14_out, not_15_out, not_16_out, not_17_out, not_18_out,
       not_19_out, not_20_out, not_21_out, not_22_out, not_23_out, not_24_out, not_25_out, not_26_out,
       not_27_out, not_28_out, not_29_out, not_30_out, not_31_out, not_32_out, not_33_out, not_34_out,
       not_35_out, not_36_out, not_37_out, not_38_out, not_39_out, not_40_out, not_41_out, not_42_out,
       not_43_out, not_44_out, not_45_out, not_46_out, not_47_out, not_48_out, not_49_out, not_50_out,
       not_51_out, not_52_out, not_53_out, not_54_out, not_55_out, not_56_out, not_57_out, not_58_out,
       not_59_out, not_60_out, not_61_out, not_62_out, not_63_out, not_64_out, not_65_out, not_66_out,
       not_67_out, not_68_out, not_69_out, not_70_out, not_71_out, not_72_out, not_73_out, not_74_out,
       not_75_out, not_76_out, not_77_out, not_78_out, not_79_out, not_80_out, not_81_out, not_82_out,
       not_83_out, not_84_out, not_85_out, not_86_out, not_87_out, not_88_out, not_89_out, not_90_out,
       not_91_out, not_92_out, not_93_out, not_94_out, not_95_out, not_96_out, not_97_out, not_98_out;

  not not_1 (not_1_out, r);
  not not_2 (not_2_out, x);
  not not_3 (not_3_out, z);
  not not_4 (not_4_out, w);
  not not_5 (not_5_out, r);
  not not_6 (not_6_out, r);
  not not_7 (not_7_out, y);
  not not_8 (not_8_out, y);
  not not_9 (not_9_out, w);
  not not_10 (not_10_out, z);
  not not_11 (not_11_out, x);
  not not_12 (not_12_out, z);
  not not_13 (not_13_out, r);
  not not_14 (not_14_out, x);
  not not_15 (not_15_out, r);
  not not_16 (not_16_out, y);
  not not_17 (not_17_out, z);
  not not_18 (not_18_out, w);
  not not_19 (not_19_out, x);
  not not_20 (not_20_out, w);
  not not_21 (not_21_out, x);
  not not_22 (not_22_out, w);
  not not_23 (not_23_out, x);
  not not_24 (not_24_out, r);
  not not_25 (not_25_out, y);
  not not_26 (not_26_out, r);
  not not_27 (not_27_out, z);
  not not_28 (not_28_out, y);
  not not_29 (not_29_out, z);
  not not_30 (not_30_out, w);
  not not_31 (not_31_out, y);
  not not_32 (not_32_out, x);
  not not_33 (not_33_out, y);
  not not_34 (not_34_out, r);
  not not_35 (not_35_out, w);
  not not_36 (not_36_out, x);
  not not_37 (not_37_out, y);
  not not_38 (not_38_out, r);
  not not_39 (not_39_out, x);
  not not_40 (not_40_out, z);
  not not_41 (not_41_out, w);
  not not_42 (not_42_out, x);
  not not_43 (not_43_out, z);
  not not_44 (not_44_out, w);
  not not_45 (not_45_out, x);
  not not_46 (not_46_out, w);
  not not_47 (not_47_out, z);
  not not_48 (not_48_out, x);
  not not_49 (not_49_out, z);
  not not_50 (not_50_out, r);
  not not_51 (not_51_out, y);
  not not_52 (not_52_out, r);
  not not_53 (not_53_out, y);
  not not_54 (not_54_out, y);
  not not_55 (not_55_out, r);
  not not_56 (not_56_out, w);
  not not_57 (not_57_out, z);
  not not_58 (not_58_out, r);
  not not_59 (not_59_out, x);
  not not_60 (not_60_out, z);
  not not_61 (not_61_out, w);
  not not_62 (not_62_out, x);
  not not_63 (not_63_out, z);
  not not_64 (not_64_out, w);
  not not_65 (not_65_out, z);
  not not_66 (not_66_out, x);
  not not_67 (not_67_out, z);
  not not_68 (not_68_out, r);
  not not_69 (not_69_out, y);
  not not_70 (not_70_out, z);
  not not_71 (not_71_out, z);
  not not_72 (not_72_out, w);
  not not_73 (not_73_out, y);
  not not_74 (not_74_out, z);
  not not_75 (not_75_out, r);
  not not_76 (not_76_out, w);
  not not_77 (not_77_out, y);
  not not_78 (not_78_out, r);
  not not_79 (not_79_out, w);
  not not_80 (not_80_out, z);
  not not_81 (not_81_out, x);
  not not_82 (not_82_out, y);
  not not_83 (not_83_out, z);
  not not_84 (not_84_out, r);
  not not_85 (not_85_out, w);
  not not_86 (not_86_out, x);
  not not_87 (not_87_out, y);
  not not_88 (not_88_out, w);
  not not_89 (not_89_out, x);
  not not_90 (not_90_out, w);
  not not_91 (not_91_out, z);
  not not_92 (not_92_out, r);
  not not_93 (not_93_out, y);
  not not_94 (not_94_out, y);
  not not_95 (not_95_out, r);
  not not_96 (not_96_out, x);
  not not_97 (not_97_out, z);
  not not_98 (not_98_out, w);
  and and_1 (and_1_out, not_1_out, not_2_out, not_3_out);
  and and_2 (and_2_out, not_4_out, y);
  and and_3 (and_3_out, not_5_out, x, z);
  and and_4 (and_4_out, not_6_out, w, not_7_out);
  and and_5 (and_5_out, w, x, not_8_out);
  and and_6 (and_6_out, r, not_9_out, not_10_out);
  and and_7 (and_7_out, r, not_11_out, z);
  and and_8 (and_8_out, r, y, not_12_out);
  and and_9 (and_9_out, not_13_out, not_14_out);
  and and_10 (and_10_out, not_15_out, not_16_out, not_17_out);
  and and_11 (and_11_out, not_18_out, not_19_out, z);
  and and_12 (and_12_out, not_20_out, not_21_out, y);
  and and_13 (and_13_out, not_22_out, y, z);
  and and_14 (and_14_out, not_23_out, y, z);
  and and_15 (and_15_out, not_24_out, w, not_25_out);
  and and_16 (and_16_out, not_26_out, w, not_27_out);
  and and_17 (and_17_out, w, not_28_out, not_29_out);
  and and_18 (and_18_out, r, x);
  and and_19 (and_19_out, not_30_out, not_31_out);
  and and_20 (and_20_out, not_32_out, not_33_out);
  and and_21 (and_21_out, not_34_out, not_35_out, x);
  and and_22 (and_22_out, w, y);
  and and_23 (and_23_out, r, not_36_out);
  and and_24 (and_24_out, r, not_37_out);
  and and_25 (and_25_out, not_38_out, not_39_out, not_40_out);
  and and_26 (and_26_out, not_41_out, not_42_out, not_43_out);
  and and_27 (and_27_out, not_44_out, not_45_out, y);
  and and_28 (and_28_out, not_46_out, y, not_47_out);
  and and_29 (and_29_out, not_48_out, y, not_49_out);
  and and_30 (and_30_out, not_50_out, x, not_51_out, z);
  and and_31 (and_31_out, not_52_out, w, not_53_out);
  and and_32 (and_32_out, w, not_54_out, z);
  and and_33 (and_33_out, not_55_out, w, x, z);
  and and_34 (and_34_out, r, not_56_out, y);
  and and_35 (and_35_out, r, x, not_57_out);
  and and_36 (and_36_out, not_58_out, not_59_out, not_60_out);
  and and_37 (and_37_out, not_61_out, not_62_out, not_63_out);
  and and_38 (and_38_out, not_64_out, y, not_65_out);
  and and_39 (and_39_out, not_66_out, y, not_67_out);
  and and_40 (and_40_out, not_68_out, w, not_69_out, not_70_out);
  and and_41 (and_41_out, r, x, not_71_out);
  and and_42 (and_42_out, not_72_out, not_73_out, not_74_out);
  and and_43 (and_43_out, not_75_out, not_76_out, x, not_77_out);
  and and_44 (and_44_out, not_78_out, not_79_out, x, not_80_out);
  and and_45 (and_45_out, w, not_81_out, not_82_out);
  and and_46 (and_46_out, w, y, not_83_out);
  and and_47 (and_47_out, not_84_out, w, x, y);
  and and_48 (and_48_out, r, not_85_out, not_86_out, y);
  and and_49 (and_49_out, r, w, not_87_out);
  and and_50 (and_50_out, not_88_out, not_89_out, y);
  and and_51 (and_51_out, not_90_out, y, not_91_out);
  and and_52 (and_52_out, not_92_out, x, not_93_out);
  and and_53 (and_53_out, w, not_94_out);
  and and_54 (and_54_out, not_95_out, w, x);
  and and_55 (and_55_out, r, not_96_out, not_97_out);
  and and_56 (and_56_out, r, not_98_out, y);
  or or_1 (a, and_1_out, and_2_out, and_3_out, and_4_out, and_5_out, and_6_out, and_7_out, and_8_out);
  or or_2 (b, and_9_out, and_10_out, and_11_out, and_12_out, and_13_out, and_14_out, and_15_out, and_16_out, and_17_out, and_18_out);
  or or_3 (c, and_19_out, and_20_out, z, and_21_out, and_22_out, and_23_out, and_24_out);
  or or_4 (d, and_25_out, and_26_out, and_27_out, and_28_out, and_29_out, and_30_out, and_31_out, and_32_out, and_33_out, and_34_out, and_35_out);
  or or_5 (e, and_36_out, and_37_out, and_38_out, and_39_out, and_40_out, and_41_out);
  or or_6 (f, and_42_out, and_43_out, and_44_out, and_45_out, and_46_out, and_47_out, and_48_out, and_49_out);
  or or_7 (g, and_50_out, and_51_out, and_52_out, and_53_out, and_54_out, and_55_out, and_56_out);
endmodule

module displaytimer2 (
  input  r,
  input  w,
  input  x,
  input  y,
  input  z,
  output a,
  output b,
  output c,
  output d,
  output e,
  output f,
  output g
);

  wire and_1_out, and_2_out, and_3_out, and_4_out, and_5_out, and_6_out, and_7_out, and_8_out, and_9_out,
       and_10_out, and_11_out, and_12_out, and_13_out, and_14_out, and_15_out, and_16_out, and_17_out,
       and_18_out, and_19_out, not_1_out, not_2_out, not_3_out, not_4_out, not_5_out, not_6_out, not_7_out,
       not_8_out, not_9_out, not_10_out, not_11_out, not_12_out, not_13_out, not_14_out, not_15_out,
       not_16_out, not_17_out, not_18_out, not_19_out, not_20_out, not_21_out, not_22_out, not_23_out,
       not_24_out, not_25_out, not_26_out, not_27_out, not_28_out;

  not not_1 (not_1_out, r);
  not not_2 (not_2_out, w);
  not not_3 (not_3_out, r);
  not not_4 (not_4_out, x);
  not not_5 (not_5_out, y);
  not not_6 (not_6_out, w);
  not not_7 (not_7_out, w);
  not not_8 (not_8_out, x);
  not not_9 (not_9_out, r);
  not not_10 (not_10_out, w);
  not not_11 (not_11_out, r);
  not not_12 (not_12_out, x);
  not not_13 (not_13_out, y);
  not not_14 (not_14_out, w);
  not not_15 (not_15_out, r);
  not not_16 (not_16_out, w);
  not not_17 (not_17_out, r);
  not not_18 (not_18_out, x);
  not not_19 (not_19_out, y);
  not not_20 (not_20_out, w);
  not not_21 (not_21_out, x);
  not not_22 (not_22_out, y);
  not not_23 (not_23_out, r);
  not not_24 (not_24_out, w);
  not not_25 (not_25_out, r);
  not not_26 (not_26_out, x);
  not not_27 (not_27_out, y);
  and and_1 (and_1_out, r, x);
  and and_2 (and_2_out, r, w);
  and and_3 (and_3_out, not_1_out, not_2_out);
  and and_4 (and_4_out, not_3_out, not_4_out, not_5_out);
  and and_5 (and_5_out, not_6_out, x);
  and and_6 (and_6_out, r, w);
  not not_28 (not_28_out, r);
  and and_7 (and_7_out, not_7_out, not_8_out);
  and and_8 (and_8_out, w, x, y);
  and and_9 (and_9_out, not_9_out, not_10_out);
  and and_10 (and_10_out, not_11_out, not_12_out, not_13_out);
  and and_11 (and_11_out, not_14_out, x);
  and and_12 (and_12_out, r, w);
  and and_13 (and_13_out, not_15_out, not_16_out);
  and and_14 (and_14_out, not_17_out, not_18_out, not_19_out);
  and and_15 (and_15_out, not_20_out, x);
  and and_16 (and_16_out, r, w, not_21_out);
  and and_17 (and_17_out, r, w, not_22_out);
  and and_18 (and_18_out, not_23_out, not_24_out);
  and and_19 (and_19_out, not_25_out, not_26_out, not_27_out);
  or or_1 (g, and_1_out, and_2_out);
  or or_2 (a, and_3_out, and_4_out, and_5_out, and_6_out);
  or or_3 (c, not_28_out, and_7_out, and_8_out);
  or or_4 (d, and_9_out, and_10_out, and_11_out, and_12_out);
  or or_5 (e, and_13_out, and_14_out, and_15_out, and_16_out, and_17_out);
  or or_6 (f, and_18_out, and_19_out);

  assign b = 1'b1;
endmodule

module _16_second_display (
  input  in_1,
  output out_2,
  output out_3,
  output out_4,
  output out_5
);

  wire clock_1_out;

  Clock clock_1 (.out(clock_1_out));
  J_K_Flip_Flop #(.trigger("falling")) j_k_ff_1 (
    .J(in_1), .clk(clock_1_out), .K(in_1), .Q(out_5));  // open: Qn, preset, en, reset
  J_K_Flip_Flop #(.trigger("falling")) j_k_ff_2 (
    .J(in_1), .clk(out_5), .K(in_1), .Q(out_4));  // open: Qn, preset, en, reset
  J_K_Flip_Flop #(.trigger("falling")) j_k_ff_3 (
    .J(in_1), .clk(out_4), .K(in_1), .Q(out_3));  // open: Qn, preset, en, reset
  J_K_Flip_Flop #(.trigger("falling")) j_k_ff_4 (
    .J(in_1), .clk(out_3), .K(in_1), .Q(out_2));  // open: Qn, preset, en, reset
endmodule

module _4bitdisplay (
  input  w,
  input  x,
  input  y,
  input  z,
  output a,
  output b,
  output c,
  output d,
  output e,
  output f,
  output g
);

  wire and_1_out, and_2_out, and_3_out, and_4_out, and_5_out, and_6_out, and_7_out, and_8_out, and_9_out,
       and_10_out, and_11_out, and_12_out, and_13_out, and_14_out, and_15_out, and_16_out, and_17_out,
       and_18_out, and_19_out, and_20_out, and_21_out, and_22_out, and_23_out, and_24_out, and_25_out,
       and_26_out, and_27_out, and_28_out, and_29_out, and_30_out, and_31_out, not_1_out, not_2_out,
       not_3_out, not_4_out, not_5_out, not_6_out, not_7_out, not_8_out, not_9_out, not_10_out, not_11_out,
       not_12_out, not_13_out, not_14_out, not_15_out, not_16_out, not_17_out, not_18_out, not_19_out,
       not_20_out, not_21_out, not_22_out, not_23_out, not_24_out, not_25_out, not_26_out, not_27_out,
       not_28_out, not_29_out, not_30_out, not_31_out, not_32_out, not_33_out, not_34_out, not_35_out,
       not_36_out, not_37_out, not_38_out, not_39_out, not_40_out, not_41_out, not_42_out, not_43_out;

  not not_1 (not_1_out, x);
  and and_1 (and_1_out, not_1_out, not_2_out);
  not not_2 (not_2_out, z);
  not not_3 (not_3_out, w);
  and and_2 (and_2_out, not_3_out, y);
  and and_3 (and_3_out, x, z);
  and and_4 (and_4_out, w, not_4_out);
  not not_4 (not_4_out, y);
  not not_5 (not_5_out, x);
  not not_6 (not_6_out, y);
  and and_5 (and_5_out, not_6_out, not_7_out);
  not not_7 (not_7_out, z);
  not not_8 (not_8_out, w);
  and and_6 (and_6_out, not_8_out, y, z);
  and and_7 (and_7_out, w, not_9_out);
  not not_9 (not_9_out, y);
  and and_8 (and_8_out, w, not_10_out);
  not not_10 (not_10_out, z);
  not not_11 (not_11_out, w);
  and and_9 (and_9_out, not_11_out, not_12_out);
  not not_12 (not_12_out, y);
  and and_10 (and_10_out, x, y);
  and and_11 (and_11_out, w, not_13_out);
  not not_13 (not_13_out, x);
  not not_14 (not_14_out, x);
  and and_12 (and_12_out, not_14_out, not_15_out);
  not not_15 (not_15_out, z);
  not not_16 (not_16_out, w);
  and and_13 (and_13_out, not_16_out, not_17_out, y);
  not not_17 (not_17_out, x);
  not not_18 (not_18_out, w);
  and and_14 (and_14_out, not_18_out, y, not_19_out);
  not not_19 (not_19_out, z);
  not not_20 (not_20_out, y);
  and and_15 (and_15_out, x, not_20_out, z);
  and and_16 (and_16_out, w, not_21_out);
  not not_21 (not_21_out, y);
  and and_17 (and_17_out, w, x, z);
  not not_22 (not_22_out, x);
  and and_18 (and_18_out, not_22_out, not_23_out);
  not not_23 (not_23_out, z);
  not not_24 (not_24_out, w);
  and and_19 (and_19_out, not_24_out, y, not_25_out);
  not not_25 (not_25_out, z);
  not not_26 (not_26_out, y);
  and and_20 (and_20_out, w, not_26_out, not_27_out);
  not not_27 (not_27_out, z);
  not not_28 (not_28_out, w);
  not not_29 (not_29_out, y);
  and and_21 (and_21_out, not_28_out, not_29_out, not_30_out);
  not not_30 (not_30_out, z);
  not not_31 (not_31_out, w);
  and and_22 (and_22_out, not_31_out, x, not_32_out);
  not not_32 (not_32_out, y);
  not not_33 (not_33_out, w);
  and and_23 (and_23_out, not_33_out, x, not_34_out);
  not not_34 (not_34_out, z);
  not not_35 (not_35_out, x);
  and and_24 (and_24_out, w, not_35_out, not_36_out);
  not not_36 (not_36_out, y);
  and and_25 (and_25_out, w, not_37_out, not_38_out);
  not not_37 (not_37_out, x);
  not not_38 (not_38_out, z);
  and and_26 (and_26_out, w, x, y);
  not not_39 (not_39_out, w);
  not not_40 (not_40_out, x);
  and and_27 (and_27_out, not_39_out, not_40_out, y);
  and and_28 (and_28_out, x, not_41_out);
  not not_41 (not_41_out, y);
  and and_29 (and_29_out, x, not_42_out);
  not not_42 (not_42_out, z);
  and and_30 (and_30_out, w, not_43_out);
  not not_43 (not_43_out, y);
  and and_31 (and_31_out, w, x);
  or or_1 (a, and_1_out, and_2_out, and_3_out, and_4_out);
  or or_2 (b, not_5_out, and_5_out, and_6_out, and_7_out, and_8_out);
  or or_3 (c, and_9_out, z, and_10_out, and_11_out);
  or or_4 (e, and_18_out, and_19_out, and_20_out);
  or or_5 (g, and_27_out, and_28_out, and_29_out, and_30_out, and_31_out);
  or or_6 (d, and_12_out, and_13_out, and_14_out, and_15_out, and_16_out, and_17_out);
  or or_7 (f, and_21_out, and_22_out, and_23_out, and_24_out, and_25_out, and_26_out);
endmodule

module _4bitdisplay1 (
  input  w,
  input  x,
  input  y,
  input  z,
  output a,
  output b,
  output c,
  output d,
  output e,
  output f,
  output g
);

  wire and_1_out, and_2_out, and_3_out, and_4_out, not_1_out, not_2_out, not_3_out, not_4_out, not_5_out,
       not_6_out, not_7_out, not_8_out, not_9_out, not_10_out, not_11_out, not_12_out;

  not not_1 (not_1_out, w);
  not not_2 (not_2_out, x);
  and and_1 (and_1_out, not_2_out, not_3_out);
  not not_3 (not_3_out, y);
  not not_4 (not_4_out, w);
  not not_5 (not_5_out, x);
  and and_2 (and_2_out, not_5_out, not_6_out);
  not not_6 (not_6_out, y);
  not not_7 (not_7_out, w);
  not not_8 (not_8_out, x);
  and and_3 (and_3_out, not_8_out, not_9_out);
  not not_9 (not_9_out, y);
  not not_10 (not_10_out, w);
  not not_11 (not_11_out, x);
  and and_4 (and_4_out, not_11_out, not_12_out);
  not not_12 (not_12_out, y);
  or or_1 (a, not_1_out, and_1_out);
  or or_2 (d, not_4_out, and_2_out);
  or or_3 (e, not_7_out, and_3_out);
  or or_4 (f, not_10_out, and_4_out);

  assign b = 1'b1;
  assign c = 1'b1;
  assign g = 1'b0;
endmodule

module _2bitcounter (
  input  in_1,
  output out_2,
  output out_3
);

  wire clock_1_out;

  Clock clock_1 (.out(clock_1_out));
  J_K_Flip_Flop j_k_ff_1 (.J(in_1), .clk(clock_1_out), .K(in_1), .Q(out_3));  // open: Qn, preset, en, reset
  J_K_Flip_Flop j_k_ff_2 (.J(in_1), .clk(out_3), .K(in_1), .Q(out_2));  // open: Qn, preset, en, reset
endmodule

module _4seconds (
  input  w,
  input  x,
  output a,
  output b,
  output c,
  output d,
  output e,
  output f,
  output g
);

  wire not_1_out, not_2_out, not_3_out, not_5_out, not_6_out;

  not not_1 (not_1_out, x);
  not not_2 (not_2_out, w);
  not not_3 (not_3_out, x);
  not not_4 (e, x);
  not not_5 (not_5_out, w);
  not not_6 (not_6_out, x);
  or or_1 (a, not_1_out, w);
  or or_2 (c, not_2_out, x);
  or or_3 (d, not_3_out, w);
  and and_1 (f, not_5_out, not_6_out);

  assign b = 1'b1;
  assign g = w;
endmodule

module _3bitcounter (
  input  in_1,
  output out_2,
  output out_3,
  output out_4
);

  wire clock_1_out;

  Clock clock_1 (.out(clock_1_out));
  J_K_Flip_Flop j_k_ff_1 (.J(in_1), .clk(clock_1_out), .K(in_1), .Q(out_4));  // open: Qn, preset, en, reset
  J_K_Flip_Flop j_k_ff_2 (.J(in_1), .clk(out_4), .K(in_1), .Q(out_3));  // open: Qn, preset, en, reset
  J_K_Flip_Flop j_k_ff_3 (.J(in_1), .clk(out_3), .K(in_1), .Q(out_2));  // open: Qn, preset, en, reset
endmodule

module _8seconds (
  input  w,
  input  x,
  input  y,
  output a,
  output b,
  output c,
  output d,
  output e,
  output f,
  output g
);

  wire and_1_out, and_2_out, and_3_out, and_4_out, and_5_out, and_6_out, and_7_out, and_8_out, and_9_out,
       and_10_out, and_11_out, and_12_out, and_13_out, and_14_out, and_15_out, and_16_out, not_1_out,
       not_2_out, not_3_out, not_4_out, not_5_out, not_6_out, not_7_out, not_8_out, not_9_out, not_10_out,
       not_11_out, not_12_out, not_13_out, not_14_out, not_15_out, not_16_out, not_17_out, not_18_out,
       not_19_out, not_20_out, not_21_out;

  not not_1 (not_1_out, w);
  not not_2 (not_2_out, y);
  not not_3 (not_3_out, x);
  not not_4 (not_4_out, y);
  not not_5 (not_5_out, x);
  not not_6 (not_6_out, w);
  not not_7 (not_7_out, y);
  not not_8 (not_8_out, w);
  not not_9 (not_9_out, y);
  not not_10 (not_10_out, x);
  not not_11 (not_11_out, w);
  not not_12 (not_12_out, y);
  not not_13 (not_13_out, y);
  not not_14 (not_14_out, x);
  not not_15 (not_15_out, y);
  not not_16 (not_16_out, x);
  not not_17 (not_17_out, y);
  not not_18 (not_18_out, w);
  not not_19 (not_19_out, x);
  not not_20 (not_20_out, y);
  and and_1 (and_1_out, not_1_out, not_2_out);
  and and_2 (and_2_out, w, y);
  not not_21 (not_21_out, w);
  and and_3 (and_3_out, not_3_out, not_4_out);
  and and_4 (and_4_out, x, y);
  or or_1 (c, not_5_out, y, w);
  and and_5 (and_5_out, not_6_out, not_7_out);
  and and_6 (and_6_out, not_8_out, x);
  and and_7 (and_7_out, x, not_9_out);
  and and_8 (and_8_out, w, not_10_out, y);
  and and_9 (and_9_out, not_11_out, not_12_out);
  and and_10 (and_10_out, x, not_13_out);
  and and_11 (and_11_out, not_14_out, not_15_out);
  and and_12 (and_12_out, w, not_16_out);
  and and_13 (and_13_out, w, not_17_out);
  and and_14 (and_14_out, not_18_out, x);
  and and_15 (and_15_out, w, not_19_out);
  and and_16 (and_16_out, w, not_20_out);
  or or_2 (a, and_1_out, x, and_2_out);
  or or_3 (b, not_21_out, and_3_out, and_4_out);
  or or_4 (d, and_5_out, and_6_out, and_7_out, and_8_out);
  or or_5 (e, and_9_out, and_10_out);
  or or_6 (f, and_11_out, and_12_out, and_13_out);
  or or_7 (g, and_14_out, and_15_out, and_16_out);
endmodule
